# Fritzing sketch sketch (saved by Fritzing 0.9.4)
breadboards: 1

parts:
  U1 = ESP32-38PinWide [part_number=ESP32-38PinWide]
  Part1 = BME280 Breakout
  SENS1 = SoilWatch 10
  Part2 = INA219 High Side DC Current Sensor Breakout [part_number=904]
  BAT1 = 18650 battery holder [package=battery-18650-kit]
  BAT2 = 18650 battery holder [package=battery-18650-kit]
  U2 = Mini-360 DC-DC Buck converter [package=THT]
  TP1 = TP4056 [chip_label=TP4056 package="DIP (Dual Inline) [THT]"]
  J1 = Power Jack [package=power_jack_smd]
  M1 = DC Motor
  D1 = Diode [package=diode-1n4148]
  R1 = Resistor [tolerance=±5% resistance=1k package=THT]
  LED1 = smd LED [color="Red (633nm)" package="0603 [SMD]"]
  Q1 = TRANSISTOR_NPN_2 [package=to-92]
  R3 = Resistor [tolerance=±5% resistance=330 package=THT]
  OMRON1 = OMRON PCB Power Relay – G5LE [part_number="G5LE-1\r\n" package=THT]
  R4 = Resistor [tolerance=±5% resistance=10k package="0402 [SMD]"]

nets:
  3.3V: U1.3.3, Part1.3.3V, Part2.VCC
  N1: U1.GPIO36, SENS1.OUT
  GND: U1.GND, Part1.GND, SENS1.GND, Part2.GND, U2.OUT-, M1.pin_1, Q1.C, R3.Pin_0
  N2: U1.GPIO13, R1.Pin_0, LED1.anode
  VIN: U1.VIN, SENS1.VCC, U2.OUT+, OMRON1.C, OMRON1.COIL2, R4.Pin_1
  N3: U1.GPIO21, Part1.SDI/SDA, Part2.SDA
  N4: U1.GPIO22, Part1.SCK/SCL, Part2.SCL
  N5: Part2.VIN-, U2.IN+
  N6: Part2.VIN+, TP1.pin3, J1.GND
  N7: BAT1.+, BAT2.+, TP1.pin4
  N8: BAT1.-, BAT2.-
  N9: U2.IN-, TP1.pin6, J1.GNDBREAK
  N10: M1.pin_2, D1.C, OMRON1.B
  N11: R1.Pin_1, Q1.B, R4.Pin_0
  N12: LED1.cathode, R3.Pin_1
  N13: Q1.E, OMRON1.COIL1

notes:
  weather sensor
  soil moisture sensor
  3.3 to 5.0 V
  current sensor
  Waterpump
  5V
  ESP32
  3.3 V input
  charge

custom parts:
  ESP32-38PinWide: Generic 38-Pin ESP32 with wide format (only access to one side of pins on a breadboard) based on Stephen Lilley's HiLetgo ESP-WROOM-32 ESP32 ESP-32S Development Board.
  SoilWatch 10: SoilWatch 10 - Capacitive soil moisture sensor
  INA219 High Side DC Current Sensor Breakout: This breakout board will solve all your power-monitoring problems. Instead of struggling with two multimeters, you can just use the handy INA219B chip on this breakout to both measure both the high side voltage and DC current draw over I2C with 1% precision. Most current-measuring devices such as our current panel meter are only good for low side measuring. That means that unless you want to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
  18650 battery holder: 18650 Battery Holder
  Mini-360 DC-DC Buck converter: Mini-360 DC-DC Buck converter. Tiny buck step down voltage converter, input voltage 4.75 to 23V output 1 to 17V adjustable. Available from ebay and the like.
  TP4056: A DIP stand-in part for whatever IC you want. With 6 pins on a 300mil dual inline package (DIP) footprint.
